// Logisim project NAND_NOR.circ as structural Verilog: 1 circuit, main circuit main
module main (
  input  A,
  input  A_2,
  input  B,
  input  B_2,
  input  A_3,
  input  A_4,
  input  B_3,
  input  B_4,
  input  A_5,
  input  A_6,
  input  B_5,
  input  B_6,
  input  A_7,
  input  A_8,
  input  B_7,
  input  B_8,
  output out_17,
  output out_18,
  output out_19,
  output out_20,
  output out_21,
  output out_22,
  output out_23,
  output out_24
);

  nand nand_1 (out_17, A, B);
  nand nand_2 (out_19, A_3, B_3);
  nor nor_1 (out_21, A_5, B_5);
  nor nor_2 (out_23, A_7, B_7);
  nand nand_3 (out_18, A_2, B_2);
  nand nand_4 (out_20, A_4, B_4);
  nor nor_3 (out_22, A_6, B_6);
  nor nor_4 (out_24, A_8, B_8);

  // Notes on the sheet:
  //   Fig 1.4.1 NAND Gate(0,0)
  //   Fig 1.4.3 NAND Gate(1,0)
  //   Fig 1.5.1 NOR Gate(0,0)
  //   Fig 1.5.3 NOR Gate(1,0)
  //   Fig 1.4.2 NAND Gate(0,1)
  //   Fig 1.4.4 NAND Gate(1,1)
  //   Fig 1.5.2 NOR Gate(0,1)
  //   Fig 1.5.4 NOR Gate(1,1)
endmodule
