// Logisim project Verification_of_Logic gates.circ as structural Verilog: 1 circuit, main circuit main
module main (
  input  in_1,
  input  in_2,
  input  A,
  input  A_2,
  input  B,
  input  B_2,
  input  A_3,
  input  A_4,
  input  B_3,
  input  B_4,
  input  A_5,
  input  A_6,
  input  B_5,
  input  B_6,
  input  A_7,
  input  A_8,
  input  B_7,
  input  B_8,
  output out_19,
  output out_20,
  output out_21,
  output out_22,
  output out_23,
  output out_24,
  output out_25,
  output out_26,
  output out_27,
  output out_28
);

  not not_1 (out_19, in_1);
  and and_1 (out_21, A, B);
  and and_2 (out_23, A_3, B_3);
  or or_1 (out_25, A_5, B_5);
  or or_2 (out_27, A_7, B_7);
  not not_2 (out_20, in_2);
  and and_3 (out_22, A_2, B_2);
  and and_4 (out_24, A_4, B_4);
  or or_3 (out_26, A_6, B_6);
  or or_4 (out_28, A_8, B_8);

  // Notes on the sheet:
  //   Fig 1.1.1 NOT Gate (input = 0)
  //   Fig 1.2.1 AND Gate(0,0)
  //   Fig 1.2.3 AND Gate(1,0)
  //   Fig 1.3.1 OR Gate(0,0)
  //   Fig 1.3.3 OR Gate(1,0)
  //   Fig 1.1.2 NOT Gate (input = 1)
  //   Fig 1.2.2 AND Gate(0,1)
  //   Fig 1.2.4 AND Gate(1,1)
  //   Fig 1.3.2 OR Gate(0,1)
  //   Fig 1.3.4 OR Gate(1,1)
endmodule
