// Logisim project XOR_XNOR.circ as structural Verilog: 1 circuit, main circuit main
module main (
  input  A,
  input  A_2,
  input  B,
  input  B_2,
  input  A_3,
  input  A_4,
  input  B_3,
  input  B_4,
  input  A_5,
  input  A_6,
  input  B_5,
  input  B_6,
  input  A_7,
  input  A_8,
  input  B_7,
  input  B_8,
  output out_17,
  output out_18,
  output out_19,
  output out_20,
  output out_21,
  output out_22,
  output out_23,
  output out_24
);

  xor xor_1 (out_17, A, B);
  xor xor_2 (out_19, A_3, B_3);
  xnor xnor_1 (out_21, A_5, B_5);
  xnor xnor_2 (out_23, A_7, B_7);
  xor xor_3 (out_18, A_2, B_2);
  xor xor_4 (out_20, A_4, B_4);
  xnor xnor_3 (out_22, A_6, B_6);
  xnor xnor_4 (out_24, A_8, B_8);

  // Notes on the sheet:
  //   Fig 1.6.1 XOR Gate(0,0)
  //   Fig 1.6.3 XOR Gate(1,0)
  //   Fig 1.7.1 XNOR Gate(0,0)
  //   Fig 1.7.3 XNOR Gate(1,0)
  //   Fig 1.6.2 XOR Gate(0,1)
  //   Fig 1.6.4 XOR Gate(1,1)
  //   Fig 1.7.2 XNOR Gate(0,1)
  //   Fig 1.7.4 XNOR Gate(1,1)
endmodule
